# Fritzing sketch debounce (saved by Fritzing 0.9.3b)
circuit board: 4.96767cm x 3.66798cm
stripboards: 1

parts:
  R1 = Resistor [tolerance=±5% resistance=10k package=THT]
  C1 = Capacitor [package=cap-pth-small2]
  R2 = Resistor [tolerance=±5% resistance=10k package=THT]
  C2 = Capacitor [package=cap-pth-small2]
  R3 = Resistor [tolerance=±5% resistance=10k package=THT]
  R4 = Resistor [tolerance=±5% resistance=10k package=THT]
  C3 = Capacitor [package=cap-pth-small2]
  C4 = Capacitor [package=cap-pth-small2]
  R5 = Resistor [tolerance=±5% resistance=10k package=THT]
  R6 = Resistor [tolerance=±5% resistance=10k package=THT]
  R7 = Resistor [tolerance=±5% resistance=10k package=THT]
  R8 = Resistor [tolerance=±5% resistance=10k package=THT]
  C5 = Capacitor [package=cap-pth-small2]
  C6 = Capacitor [package=cap-pth-small2]
  C7 = Capacitor [package=cap-pth-small2]
  C8 = Capacitor [package=cap-pth-small2]
  J1_-_Pi = male pin header, 12 pins [form="♂ (male)"]
  J2_-_Buttons = male pin header, 11 pins [form="♂ (male)"]
  R9 = Resistor [tolerance=±5% resistance=10k package=THT]
  R10 = Resistor [tolerance=±5% resistance=10k package=THT]
  C9 = Capacitor [package=cap-pth-small2]
  C10 = Capacitor [package=cap-pth-small2]

nets:
  N1: R1.Pin_0, C1.2, J1_-_Pi.pin7
  N2: R1.Pin_1, J2_-_Buttons.pin6
  N3: C1.1, C2.1, C3.1, C4.1, C5.2, C6.2, C7.2, C8.2, J1_-_Pi.pin2, J2_-_Buttons.pin1, C9.1, C10.2
  N4: R2.Pin_0, C2.2, J1_-_Pi.pin6
  N5: R2.Pin_1, J2_-_Buttons.pin5
  N6: R3.Pin_0, C3.2, J1_-_Pi.pin5
  N7: R3.Pin_1, J2_-_Buttons.pin4
  N8: R4.Pin_0, C4.2, J1_-_Pi.pin4
  N9: R4.Pin_1, J2_-_Buttons.pin3
  N10: R5.Pin_0, C5.1, J1_-_Pi.pin8
  N11: R5.Pin_1, J2_-_Buttons.pin7
  N12: R6.Pin_0, C7.1, J1_-_Pi.pin10
  N13: R6.Pin_1, J2_-_Buttons.pin9
  N14: R7.Pin_0, C8.1, J1_-_Pi.pin11
  N15: R7.Pin_1, J2_-_Buttons.pin10
  N16: R8.Pin_0, C6.1, J1_-_Pi.pin9
  N17: R8.Pin_1, J2_-_Buttons.pin8
  N18: J1_-_Pi.pin3, R10.Pin_0, C9.2
  N19: J1_-_Pi.pin12, R9.Pin_0, C10.1
  N20: J2_-_Buttons.pin2, R10.Pin_1
  N21: J2_-_Buttons.pin11, R9.Pin_1
