# Fritzing sketch micro (saved by Fritzing 0.9.3b)
circuit board: 8.46667cm x 5.64444cm
breadboards: 1

parts:
  Pro_mini = Arduino Pro Mini v13
  Teensy_3_1 = Teensy 3.1
  UART = male pin header, 2 pins [form="♂ (male)"]
  ISP = male pin header, 4 pins [form="♂ (male)"]
  I2C = male pin header, 2 pins [form="♂ (male)"]
  IO = male pin header, 8 pins [form="♂ (male)"]
  Vin = male pin header, 3 pins [form="♂ (male)"]

nets:
  N1: Pro_mini.D0/TX, Teensy_3_1.D1, UART.pin2
  N2: Pro_mini.D1/RX, Teensy_3_1.D0, UART.pin1
  VCC: Pro_mini.VCC, Teensy_3_1.Vin, Vin.pin3
  GND: Pro_mini.GND, Teensy_3_1.GND, Vin.pin1
  N3: Pro_mini.A4, Teensy_3_1.A0/D14, I2C.pin2
  N4: Pro_mini.A5, Teensy_3_1.A1/D15, I2C.pin1
  N5: Pro_mini.D13/SCK, Teensy_3_1.D13, ISP.pin2
  N6: Pro_mini.D12/MISO, Teensy_3_1.D11, ISP.pin3
  N7: Pro_mini.D11_PWM/MOSI, Teensy_3_1.D12, ISP.pin4
  N8: Pro_mini.D10_PWM/SS, Teensy_3_1.D10, ISP.pin1
  N9: Pro_mini.D9_PWM, Teensy_3_1.D9, IO.pin8
  N10: Pro_mini.D8, Teensy_3_1.D8, IO.pin7
  N11: Pro_mini.D7, Teensy_3_1.D7, IO.pin6
  N12: Pro_mini.D6_PWM, Teensy_3_1.D6, IO.pin5
  N13: Pro_mini.D5_PWM, Teensy_3_1.D5, IO.pin4
  N14: Pro_mini.D4, Teensy_3_1.D4, IO.pin3
  N15: Pro_mini.D3_PWM, Teensy_3_1.D3, IO.pin2
  N16: Pro_mini.D2, Teensy_3_1.D2, IO.pin1
